// Logisim project Controleur.circ as structural Verilog: 3 circuits, main circuit main
module main (
  input  [7:0] in_1,
  input  in_2,
  output [2:0] Rd,
  output [2:0] Rm,
  output [2:0] Rn,
  output [3:0] Opcode,
  output LoadStore,
  output Shift,
  output Sel
);

  wire Clock_out;
  wire [7:0] adder_1_out, PC_q;
  wire [15:0] RI_q, rom_1_data;

  ROM #(.dataWidth(16)) rom_1 (.addr(PC_q), .data(rom_1_data));
  Register #(.width(16)) RI (.D(rom_1_data), .en(in_2), .clk(Clock_out), .Q(RI_q));  // open: clr
  Clock Clock (.out(Clock_out));
  Adder adder_1 (.a(PC_q), .b(in_1), .out(adder_1_out));  // open: cin, cout
  Register PC (.D(adder_1_out), .en(in_2), .clk(Clock_out), .Q(PC_q));  // open: clr
  // DataProcessing dataprocessing_1: pin names not known; wires that end beside it: Rd, Rm, Rn, Opcode, LoadStore, Shift

  // Notes on the sheet:
  //   contents of rom_1 (hex, n*v repeats v):
  //   1 10 11 100 101 110 111 1000 1001 1011 1100 1101 1100 1101 1110 1111
endmodule

module Controleur (
  input  [5:0] DataProcessing,
  input  [15:0] PC
);

  wire comparator_1_eq, multiplexer_1_out;

  Comparator #(.width(6)) comparator_1 (.a(PC[15:10]), .b(DataProcessing), .eq(comparator_1_eq));  // open: gt, lt
  Multiplexer #(.enable("false")) multiplexer_1 (.out(multiplexer_1_out), .sel(comparator_1_eq));  // open: in0, in1

  // Other names for the same wires on the sheet: OpCode[5:0] = PC[15:10]; b0 = PC[0]; b1 = PC[1]; b2 = PC[2];
  //   b3 = PC[3]; b4 = PC[4]; b5 = PC[5]; b6 = PC[6]; b7 = PC[7]; b8 = PC[8]; b9 = PC[9]
endmodule

module DataProcessing (
  input  [15:0] PC,
  input  [5:0] in_2,
  input  [2:0] in_3,
  input  [1:0] in_4,
  input  [2:0] in_5,
  input  [2:0] in_6,
  input  [3:0] in_7,
  input  [3:0] in_8,
  input  in_9,
  input  [9:0] in_10,
  output [2:0] Rd,
  output [2:0] Rm,
  output [2:0] Rn,
  output [3:0] ULACode,
  output LoadStore,
  output Shift,
  output Sel
);

  wire and_1_out, comparator_3_eq, comparator_4_eq, comparator_5_eq, comparator_8_eq,
       ExceptionDataProcessing, isBranch, isDataProcessing, isLoad, isNOP, isShift, not_1_out, not_2_out,
       not_3_out, not_4_out;
  wire [5:3] Answer;

  Comparator #(.width(6)) comparator_1 (.a(PC[15:10]), .b(in_2), .eq(isDataProcessing));  // open: gt, lt
  Comparator #(.width(2)) comparator_2 (.a(PC[15:14]), .b(in_4), .eq(isShift));  // open: gt, lt
  Comparator #(.width(3)) comparator_3 (.a(in_5), .b(PC[15:13]), .eq(comparator_3_eq));  // open: gt, lt
  Comparator #(.width(3)) comparator_4 (.a(PC[15:13]), .b(in_6), .eq(comparator_4_eq));  // open: gt, lt
  Comparator #(.width(4)) comparator_5 (.a(PC[15:12]), .b(in_7), .eq(comparator_5_eq));  // open: gt, lt
  Comparator #(.width(4)) comparator_6 (.a(PC[15:12]), .b(in_8), .eq(isBranch));  // open: gt, lt
  not not_1 (not_1_out, isDataProcessing);
  not not_2 (not_2_out, isShift);
  not not_3 (not_3_out, isLoad);
  not not_4 (not_4_out, isBranch);
  or or_1 (isLoad, comparator_3_eq, comparator_4_eq, comparator_5_eq);
  and and_1 (and_1_out, not_1_out, not_2_out, not_3_out, not_4_out);
  Comparator #(.width(1)) comparator_7 (.a(and_1_out), .b(in_9), .eq(isNOP));  // open: gt, lt
  Multiplexer #(.width(3), .enable("false")) multiplexer_1 (
    .in0(Answer), .in1(Rd), .out(Rm), .sel(ExceptionDataProcessing));
  Multiplexer #(.width(3), .enable("false")) multiplexer_2 (
    .in0(Rd), .in1(Answer), .out(Rn), .sel(ExceptionDataProcessing));
  Multiplexer #(.enable("false")) multiplexer_3 (.in0(1'b0), .in1(1'b1), .out(Shift), .sel(isShift));
  Comparator #(.width(3)) comparator_8 (.a({PC[6], PC[7], PC[9]}), .b(in_3), .eq(comparator_8_eq));  // open: gt, lt
  and and_2 (ExceptionDataProcessing, comparator_8_eq, isDataProcessing);
  Multiplexer #(.width(10), .enable("false")) multiplexer_4 (
    .in0(PC[9:0]), .in1(in_10), .out({ULACode, Answer, Rd}), .sel(isNOP));

  assign LoadStore = 1'b0;
  assign Sel = 1'b0;

  // Other names for the same wires on the sheet: checkBL[3:0] = PC[15:12]; CheckLoad[2:0] = PC[15:13];
  //   OpCodeData[5:0] = PC[15:10]; CheckShift[1:0] = PC[15:14]; DataCode[9:0] = PC[9:0];
  //   Change[2:0] = {PC[6], PC[7], PC[9]}; Answer (some bits) = {ULACode, Rd}

  // Notes on the sheet:
  //   Opcode of DataProcessing only if the opcode = 010000
  //   Opcode of Shift only if the opcode = 00xxxx
  //   Opcode of Branch only if the opcode = 00xxxx
  //   Opcode of Load only if the opcode = 0101xx or 011xxx or 1000xxx
  //   Its not a operation available if the opcode its diferent of the shift, data processing, load or conditional branch:
  //   1001
  //   Exception to change RM and RN when:
  //   ReverseSubtractFrom0 and MultiplyTwoRegisters :
  //   Putted a OR because I already know its imposible be more than 1 of 3 options in the same time.
  //   1101
  //   1 only to Ld/S
  //   if its with a not validate opcode, it will:
  //   set all the other information/bits to 0 (to imply a "error")
endmodule
